# Fritzing sketch Bike circuit (saved by Fritzing 0.9.3b)
breadboards: 1

parts:
  part = Arduino Nano (Rev3.0)
  Left_Back_RGB_Strip_(WS2812) = SMD RGB LED (WS2812) [package=5050]
  Right_Back_RGB_Strip_(WS2812) = SMD RGB LED (WS2812) [package=5050]
  Q1 = NPN-Transistor [package="TO92 [THT]"]
  S1 = Round Pushbutton
  U1 = Vibration Motor- ROB-08449 [package=vibe-motor-10mm]
  R1 = Resistor [tolerance=±5% resistance=1k package=THT]
  S2 = Round Pushbutton
  GY-521 = Grove 3 Axis Digital Accelerometer 16g
  Right_Front_RGB_Strip_(WS2812) = SMD RGB LED (WS2812) [package=5050]
  Left_Front_RGB_Strip_(WS2812) = SMD RGB LED (WS2812) [package=5050]

nets:
  VSS: part.GND, Left_Back_RGB_Strip_(WS2812).VSS, Right_Back_RGB_Strip_(WS2812).VSS, Q1.E, S1.leg0, S2.leg0, GY-521.GND, Right_Front_RGB_Strip_(WS2812).VSS, Left_Front_RGB_Strip_(WS2812).VSS
  N1: part.D2, Left_Front_RGB_Strip_(WS2812).DIn
  N2: part.D3, Right_Front_RGB_Strip_(WS2812).DIn
  N3: part.D4, Left_Back_RGB_Strip_(WS2812).DIn
  N4: part.D5, Right_Back_RGB_Strip_(WS2812).DIn
  N5: part.D6, S2.leg1
  N6: part.D7, S1.leg1
  N7: part.D8, R1.Pin_1
  VCC: part.5V, Left_Back_RGB_Strip_(WS2812).VCC, Right_Back_RGB_Strip_(WS2812).VCC, U1.+, GY-521.VCC, Right_Front_RGB_Strip_(WS2812).VCC, Left_Front_RGB_Strip_(WS2812).VCC
  N8: part.A5, GY-521.SCL
  N9: part.A4, GY-521.SDA
  N10: Q1.B, R1.Pin_0
  N11: Q1.C, U1.-
